# Fritzing sketch force press sound (saved by Fritzing 0.9.4)
breadboards: 1

parts:
  Part1 = Arduino Nano 33 BLE Sense
  R1 = Resistor [tolerance=±5% resistance=220 package="0805 [SMD]"]
  J1 = Basic Force Sensing Resistor (FSR) [package=THT]
  R2 = Resistor [tolerance=±5% resistance=220 package="0805 [SMD]"]
  SP1 = SPEAKER [package=pcb_mount_speaker]

nets:
  N1: Part1.GND, R1.Pin_1, R2.Pin_1, SP1.+
  N2: Part1.D9, SP1.-
  N3: Part1.D12, R1.Pin_0
  N4: Part1.A0, J1.pin_0, R2.Pin_0
  N5: Part1.+3V3, J1.pin_1

custom parts:
  Arduino Nano 33 BLE Sense: The Arduino Nano 33 BLE Sense is a completely new board on a well-known form factor. It comes with 9 axis inertal sensor, humidity, temperature sensor, barometric sensor, microphone gesture, proximity, light color and light intensity sensor.
