# Fritzing sketch force press (saved by Fritzing 0.9.4)
breadboards: 1

parts:
  Part1 = Arduino Nano 33 BLE Sense
  R1 = Resistor [tolerance=±5% resistance=220 package="0805 [SMD]"]
  J1 = Basic Force Sensing Resistor (FSR) [package=THT]
  Part2 = LED Sequin - Emerald Green [part_number=1756]
  Part3 = LED Sequin - Warm White [part_number=1758]
  R2 = Resistor [tolerance=±5% resistance=220 package="0805 [SMD]"]

nets:
  N1: Part1.GND, R1.Pin_1, Part2.-, Part3.-, R2.Pin_1
  N2: Part1.D6, Part3.+
  N3: Part1.D9, Part2.+
  N4: Part1.D12, R1.Pin_0
  N5: Part1.A0, J1.pin_0, R2.Pin_0
  N6: Part1.+3V3, J1.pin_1

custom parts:
  Arduino Nano 33 BLE Sense: The Arduino Nano 33 BLE Sense is a completely new board on a well-known form factor. It comes with 9 axis inertal sensor, humidity, temperature sensor, barometric sensor, microphone gesture, proximity, light color and light intensity sensor.
  LED Sequin - Emerald Green: Sew a little sparkle into your wearable project with an Adafruit LED Sequin. Simply connect 3 to 6VDC to the + pin and ground to the - pin, and the LED on the board will light up. You can make the LEDs fade and twinkle by using PWM.
  LED Sequin - Warm White: Sew a little sparkle into your wearable project with an Adafruit LED Sequin. Simply connect 3 to 6VDC to the + pin and ground to the - pin, and the LED on the board will light up. You can make the LEDs fade and twinkle by using PWM.
