# Fritzing sketch projec 2 Sketch 2 (saved by Fritzing 0.9.4)
breadboards: 1

parts:
  Part1 = Arduino Nano (Rev3.0)
  S1 = Pushbutton [package="[SMD]"]
  S2 = Pushbutton [package="[SMD]"]
  S3 = Pushbutton [package="[SMD]"]
  S4 = Pushbutton [package="[SMD]"]
  R1 = Resistor [tolerance=±5% resistance=220 package="0603 [SMD]"]
  R2 = Resistor [tolerance=±5% resistance=220 package="0603 [SMD]"]
  R3 = Resistor [tolerance=±5% resistance=220 package="0603 [SMD]"]
  R4 = Resistor [tolerance=±5% resistance=220 package="0603 [SMD]"]

nets:
  N1: Part1.D2, Part1.D3, Part1.D4, Part1.D5, S1.Pin_1, S1.Pin_2, S2.Pin_1, S2.Pin_2, S3.Pin_1, S3.Pin_2, S4.Pin_1, S4.Pin_2
  N2: S1.Pin_3, S1.Pin_4, R4.Pin_0
  N3: S2.Pin_3, S2.Pin_4, R3.Pin_0
  N4: S3.Pin_3, S3.Pin_4, R2.Pin_0
  N5: S4.Pin_3, S4.Pin_4, R1.Pin_0
  N6: R1.Pin_1, R2.Pin_1, R3.Pin_1, R4.Pin_1
