# Fritzing sketch projec 2 Sketch (saved by Fritzing 0.9.4)
breadboards: 1

parts:
  S1 = Pushbutton [package="[SMD]"]
  S2 = Pushbutton [package="[SMD]"]
  S3 = Pushbutton [package="[SMD]"]
  S4 = Pushbutton [package="[SMD]"]
  R1 = Resistor [tolerance=±5% resistance=220 package="0603 [SMD]"]
  R2 = Resistor [tolerance=±5% resistance=220 package="0603 [SMD]"]
  R3 = Resistor [tolerance=±5% resistance=220 package="0603 [SMD]"]
  R4 = Resistor [tolerance=±5% resistance=220 package="0603 [SMD]"]
  Part2 = Arduino Nano 33 IOT

nets:
  N1: S1.Pin_1, S1.Pin_2, S2.Pin_1, S2.Pin_2, S3.Pin_1, S3.Pin_2, S4.Pin_1, S4.Pin_2, Part2.D2, Part2.D3~, Part2.D4, Part2.D5~
  N2: S1.Pin_3, S1.Pin_4, R4.Pin_0
  N3: S2.Pin_3, S2.Pin_4, R3.Pin_0
  N4: S3.Pin_3, S3.Pin_4, R2.Pin_0
  N5: S4.Pin_3, S4.Pin_4, R1.Pin_0
  N6: R1.Pin_1, R2.Pin_1, R3.Pin_1, R4.Pin_1
  N7: Part2.RESET, Part2.A7
  N8: Part2.GND, Part2.D13~
  N9: Part2.D11/MOSI, Part2.+5V

custom parts:
  Arduino Nano 33 IOT: The Arduino Nano 33 IoT is the easiest and cheapest point of entry to enhance existing devices (and creating new ones) to be part of the IoT and designing pico-network applications. Whether you are looking at building a sensor network connected to your office or home router, or if you want to create a BLE device sending data to a cellphone, the Nano 33 IoT is your one-stop-solution for many of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
